// Logisim project Project3Given.circ as structural Verilog: 9 circuits, main circuit CPU15
module main (
  input  EnableBreakpoint,
  input  [14:0] Breakpoint
);

  wire and_2_out, and_3_out, chipset_1_irq, CLK, clock_1_out, cpu15_1_c, cpu15_1_e, cpu15_1_i, cpu15_1_n,
       cpu15_1_o, cpu15_1_z, KBCLR, KBIRQ, KBRD, MEMCS, nand_1_out, RE, TTYCLR, TTYWE, WE;
  wire [6:0] KBDATA, TTYDATA;
  wire [7:0] cpu15_1_srf;
  wire [14:0] ADDR, chipset_1_ivect, chipset_1_led0, chipset_1_led1, chipset_1_led2, chipset_1_led3,
       chipset_1_led4, chipset_1_led5, chipset_1_led6, chipset_1_led7, chipset_1_led8, chipset_1_led9,
       chipset_1_leda, chipset_1_ledb, chipset_1_ledc, chipset_1_ledd, chipset_1_lede, cpu15_1_ib,
       cpu15_1_pc, cpu15_1_r0, cpu15_1_r1, cpu15_1_r2, cpu15_1_r3, cpu15_1_r4, cpu15_1_r5, cpu15_1_r6,
       cpu15_1_r7, cpu15_1_srp, DATA, xnor_1_out;

  Clock clock_1 (.out(clock_1_out));
  nand nand_1 (nand_1_out, EnableBreakpoint, xnor_1_out[0], xnor_1_out[1], xnor_1_out[2], xnor_1_out[3], xnor_1_out[4], xnor_1_out[5], xnor_1_out[6], xnor_1_out[7], xnor_1_out[8], xnor_1_out[9], xnor_1_out[10], xnor_1_out[11], xnor_1_out[12], xnor_1_out[13], xnor_1_out[14], 1'b1);
  and and_1 (CLK, clock_1_out, nand_1_out);
  assign xnor_1_out = ~(Breakpoint ^ cpu15_1_pc);  // XNOR_Gate xnor_1, 15 bits wide
  LED I (.in(cpu15_1_i));
  LED Z (.in(cpu15_1_z));
  LED N (.in(cpu15_1_n));
  LED O (.in(cpu15_1_o));
  LED C (.in(cpu15_1_c));
  LED E (.in(cpu15_1_e));
  and and_2 (and_2_out, WE, MEMCS);
  and and_3 (and_3_out, MEMCS, RE);
  RAM #(.addrWidth(15), .asyncread("true"), .dataWidth(15), .databus("bidir")) ram_1 (
    .addr(ADDR), .we(and_2_out), .oe(and_3_out), .clk(CLK), .data(DATA));
  // Probe on cpu15_1_pc
  // Probe on cpu15_1_ib
  // Probe on cpu15_1_srp
  // Probe on cpu15_1_srf
  // Probe on cpu15_1_r0
  // Probe on cpu15_1_r1
  // Probe on cpu15_1_r2
  // Probe on cpu15_1_r3
  // Probe on cpu15_1_r4
  // Probe on cpu15_1_r5
  // Probe on cpu15_1_r6
  // Probe on cpu15_1_r7
  CPU15 cpu15_1 (
    .I(cpu15_1_i), .Z(cpu15_1_z), .N(cpu15_1_n), .O(cpu15_1_o), .C(cpu15_1_c), .E(cpu15_1_e),
    .PC(cpu15_1_pc), .IB(cpu15_1_ib), .SRP(cpu15_1_srp), .SRF(cpu15_1_srf), .R0(cpu15_1_r0), .R1(cpu15_1_r1),
    .R2(cpu15_1_r2), .R3(cpu15_1_r3), .R4(cpu15_1_r4), .R5(cpu15_1_r5), .R6(cpu15_1_r6), .R7(cpu15_1_r7),
    .CLK(CLK), .IRQ(chipset_1_irq), .RE(RE), .WE(WE), .ADDR(ADDR), .DATAIN(DATA), .DATAOUT(DATA));
  // Probe on ADDR
  // Probe on DATA
  // Probe on chipset_1_ivect
  // Probe on TTYDATA
  CHIPSET chipset_1 (
    .RE(RE), .WE(WE), .ADDR(ADDR), .CPUDATAIN(DATA), .CPUDATAOUT(DATA), .IRQ(chipset_1_irq),
    .IVECT(chipset_1_ivect), .CLK(CLK), .MEMCS(MEMCS), .TTYWR(TTYWE), .TTYCLR(TTYCLR), .TTYDATA(TTYDATA),
    .KBRD(KBRD), .KBCLR(KBCLR), .KBIRQ(KBIRQ), .KBDATA(KBDATA), .LED0(chipset_1_led0), .LED1(chipset_1_led1),
    .LED2(chipset_1_led2), .LED3(chipset_1_led3), .LED4(chipset_1_led4), .LED5(chipset_1_led5),
    .LED6(chipset_1_led6), .LED7(chipset_1_led7), .LED8(chipset_1_led8), .LED9(chipset_1_led9),
    .LEDA(chipset_1_leda), .LEDB(chipset_1_ledb), .LEDC(chipset_1_ledc), .LEDD(chipset_1_ledd),
    .LEDE(chipset_1_lede));
  TTY tty_1 (.data(TTYDATA), .clk(CLK), .we(TTYWE), .clr(TTYCLR));
  Keyboard keyboard_1 (.clk(CLK), .re(KBRD), .clr(KBCLR), .avail(KBIRQ), .data(KBDATA));
  DotMatrix #(.matrixcols(15), .matrixrows(15)) dotmatrix_1 (
    .col0(chipset_1_led0), .col1(chipset_1_led1), .col2(chipset_1_led2), .col3(chipset_1_led3),
    .col4(chipset_1_led4), .col5(chipset_1_led5), .col6(chipset_1_led6), .col7(chipset_1_led7),
    .col8(chipset_1_led8), .col9(chipset_1_led9), .col10(chipset_1_leda), .col11(chipset_1_ledb),
    .col12(chipset_1_ledc), .col13(chipset_1_ledd), .col14(chipset_1_lede));
endmodule

// CPU
module CPU15 (
  input  [14:0] DATAIN,
  input  CLK,
  input  IRQ,
  output [14:0] PC,
  output [14:0] IB,
  output [14:0] SRP,
  output [7:0] SRF,
  output [14:0] R0,
  output [14:0] R1,
  output [14:0] R2,
  output [14:0] R3,
  output [14:0] R4,
  output [14:0] R5,
  output [14:0] R6,
  output [14:0] R7,
  output RE,
  output WE,
  output I,
  output Z,
  output [14:0] ADDR,
  output N,
  output O,
  output C,
  output E,
  output [14:0] DATAOUT
);


  // Other names for the same wires on the sheet: DATA[14:0] = DATAIN
endmodule

module CHIPSET (
  input  RE,
  input  WE,
  input  [14:0] ADDR,
  input  [14:0] CPUDATAIN,
  input  KBIRQ,
  input  [6:0] KBDATA,
  input  CLK,
  output MEMCS,
  output TTYWR,
  output [14:0] IVECT,
  output TTYCLR,
  output [6:0] TTYDATA,
  output KBRD,
  output KBCLR,
  output [14:0] CPUDATAOUT,
  output IRQ,
  output [14:0] LED0,
  output [14:0] LED1,
  output [14:0] LED2,
  output [14:0] LED3,
  output [14:0] LED4,
  output [14:0] LED5,
  output [14:0] LED6,
  output [14:0] LED7,
  output [14:0] LED8,
  output [14:0] LED9,
  output [14:0] LEDA,
  output [14:0] LEDB,
  output [14:0] LEDC,
  output [14:0] LEDD,
  output [14:0] LEDE
);

  wire and_1_out, and_8_out, and_10_out, DATA7, IOCS, IVECTADDR, IVECTEN, IVECTRE, KBCS, LED0EN, LED0END,
       LED1EN, LED1END, LED2EN, LED2END, LED3EN, LED3END, LED4EN, LED4END, LED5EN, LED5END, LED6EN, LED6END,
       LED7EN, LED7END, LED8EN, LED8END, LED9EN, LED9END, LEDAEN, LEDAEND, LEDBEN, LEDBEND, LEDCEN, LEDCEND,
       LEDCS, LEDDEN, LEDDEND, LEDEEN, LEDEEND, LEDFEND, LEDRE, multiplexer_17_out, multiplexer_18_out, RWE,
       TTYCS;
  wire [14:0] DATAL0, DATAL1, DATAL2, DATAL3, DATAL4, DATAL5, DATAL6, DATAL7, DATAL8, DATAL9, DATALA, DATALB,
       DATALC, DATALD, DATALE, LEDDATA;
  wire [14:8] KBDATA15;

  assign CPUDATAOUT = KBRD ? {KBDATA15, DATA7, KBDATA} : 15'bz;  // Controlled_Buffer controlled_buffer_1
  assign CPUDATAOUT = LEDRE ? LEDDATA : 15'bz;  // Controlled_Buffer controlled_buffer_2
  assign CPUDATAOUT = IVECTRE ? IVECT : 15'bz;  // Controlled_Buffer controlled_buffer_3
  Register #(.width(15)) register_1 (.D(DATAL0), .en(LED0EN), .Q(LED0), .clk(CLK));  // open: clr
  Register #(.width(15)) register_2 (.D(DATAL1), .en(LED1EN), .Q(LED1), .clk(CLK));  // open: clr
  Register #(.width(15)) register_3 (.D(DATAL2), .en(LED2EN), .Q(LED2), .clk(CLK));  // open: clr
  Register #(.width(15)) register_4 (.D(DATAL3), .en(LED3EN), .Q(LED3), .clk(CLK));  // open: clr
  Register #(.width(15)) register_5 (.D(DATAL4), .en(LED4EN), .Q(LED4), .clk(CLK));  // open: clr
  and and_1 (and_1_out, WE, LEDCS);
  Decoder #(.select(4)) decoder_1 (
    .out0(LED0END), .out1(LED1END), .out2(LED2END), .out3(LED3END), .out4(LED4END), .out5(LED5END),
    .out6(LED6END), .out7(LED7END), .out8(LED8END), .out9(LED9END), .out10(LEDAEND), .out11(LEDBEND),
    .out12(LEDCEND), .out13(LEDDEND), .out14(LEDEEND), .out15(LEDFEND), .sel(ADDR[3:0]), .en(and_1_out));
  Register #(.width(15)) register_6 (.D(DATAL5), .en(LED5EN), .Q(LED5), .clk(CLK));  // open: clr
  Register #(.width(15)) register_7 (.D(DATAL6), .en(LED6EN), .Q(LED6), .clk(CLK));  // open: clr
  Register #(.width(15)) register_8 (.D(DATAL7), .en(LED7EN), .Q(LED7), .clk(CLK));  // open: clr
  Register #(.width(15)) register_9 (.D(DATAL8), .en(LED8EN), .Q(LED8), .clk(CLK));  // open: clr
  Register #(.width(15)) register_10 (.D(DATAL9), .en(LED9EN), .Q(LED9), .clk(CLK));  // open: clr
  or or_1 (LED0EN, LED0END, LEDFEND);
  or or_2 (LED1EN, LED1END, LEDFEND);
  or or_3 (LED2EN, LED2END, LEDFEND);
  or or_4 (LED3EN, LED3END, LEDFEND);
  or or_5 (LED4EN, LED4END, LEDFEND);
  or or_6 (LED5EN, LED5END, LEDFEND);
  or or_7 (LED6EN, LED6END, LEDFEND);
  or or_8 (LED7EN, LED7END, LEDFEND);
  or or_9 (LED8EN, LED8END, LEDFEND);
  or or_10 (LED9EN, LED9END, LEDFEND);
  or or_11 (LEDAEN, LEDAEND, LEDFEND);
  or or_12 (LEDBEN, LEDBEND, LEDFEND);
  or or_13 (LEDCEN, LEDCEND, LEDFEND);
  or or_14 (LEDDEN, LEDDEND, LEDFEND);
  or or_15 (LEDEEN, LEDEEND, LEDFEND);
  Pull_Resistor pull_resistor_1 (.node(KBDATA15[14]));
  Pull_Resistor pull_resistor_2 (.node(KBDATA15[13]));
  Pull_Resistor pull_resistor_3 (.node(KBDATA15[12]));
  Pull_Resistor pull_resistor_4 (.node(KBDATA15[11]));
  Pull_Resistor pull_resistor_5 (.node(KBDATA15[10]));
  Pull_Resistor pull_resistor_6 (.node(KBDATA15[9]));
  Pull_Resistor pull_resistor_7 (.node(KBDATA15[8]));
  Pull_Resistor pull_resistor_8 (.node(DATA7));
  Register #(.width(15)) register_11 (.D(DATALA), .en(LEDAEN), .Q(LEDA), .clk(CLK));  // open: clr
  Register #(.width(15)) register_12 (.D(DATALB), .en(LEDBEN), .Q(LEDB), .clk(CLK));  // open: clr
  Register #(.width(15)) register_13 (.D(DATALC), .en(LEDCEN), .Q(LEDC), .clk(CLK));  // open: clr
  Register #(.width(15)) register_14 (.D(DATALD), .en(LEDDEN), .Q(LEDD), .clk(CLK));  // open: clr
  Register #(.width(15)) register_15 (.D(DATALE), .en(LEDEEN), .Q(LEDE), .clk(CLK));  // open: clr
  Multiplexer #(.width(15)) multiplexer_1 (.in0(CPUDATAIN), .in1(LED1), .out(DATAL0), .sel(LEDFEND));
  Multiplexer #(.width(15)) multiplexer_2 (.in0(CPUDATAIN), .in1(LED2), .out(DATAL1), .sel(LEDFEND));
  Multiplexer #(.width(15)) multiplexer_3 (.in0(CPUDATAIN), .in1(LED3), .out(DATAL2), .sel(LEDFEND));
  Multiplexer #(.width(15)) multiplexer_4 (.in0(CPUDATAIN), .in1(LED4), .out(DATAL3), .sel(LEDFEND));
  Multiplexer #(.width(15)) multiplexer_5 (.in0(CPUDATAIN), .in1(LED5), .out(DATAL4), .sel(LEDFEND));
  Multiplexer #(.select(4), .width(15)) multiplexer_6 (
    .in0(LED0), .in1(LED1), .in2(LED2), .in3(LED3), .in4(LED4), .in5(LED5), .in6(LED6), .in7(LED7),
    .in8(LED8), .in9(LED9), .in10(LEDA), .in11(LEDB), .in12(LEDC), .in13(LEDD), .in14(LEDE),
    .in15({15{1'b0}}), .out(LEDDATA), .sel(ADDR[3:0]));
  Multiplexer #(.width(15)) multiplexer_7 (.in0(CPUDATAIN), .in1(LED6), .out(DATAL5), .sel(LEDFEND));
  Multiplexer #(.width(15)) multiplexer_8 (.in0(CPUDATAIN), .in1(LED7), .out(DATAL6), .sel(LEDFEND));
  Multiplexer #(.width(15)) multiplexer_9 (.in0(CPUDATAIN), .in1(LED8), .out(DATAL7), .sel(LEDFEND));
  Multiplexer #(.width(15)) multiplexer_10 (.in0(CPUDATAIN), .in1(LED9), .out(DATAL8), .sel(LEDFEND));
  Multiplexer #(.width(15)) multiplexer_11 (.in0(CPUDATAIN), .in1(LEDA), .out(DATAL9), .sel(LEDFEND));
  and and_2 (LEDRE, RE, LEDCS);
  Multiplexer #(.width(15)) multiplexer_12 (.in0(CPUDATAIN), .in1(LEDB), .out(DATALA), .sel(LEDFEND));
  Multiplexer #(.width(15)) multiplexer_13 (.in0(CPUDATAIN), .in1(LEDC), .out(DATALB), .sel(LEDFEND));
  Multiplexer #(.width(15)) multiplexer_14 (.in0(CPUDATAIN), .in1(LEDD), .out(DATALC), .sel(LEDFEND));
  Multiplexer #(.width(15)) multiplexer_15 (.in0(CPUDATAIN), .in1(LEDE), .out(DATALD), .sel(LEDFEND));
  Multiplexer #(.width(15)) multiplexer_16 (.in0(CPUDATAIN), .in1(CPUDATAIN), .out(DATALE), .sel(LEDFEND));
  and and_3 (IOCS, ADDR[5], ADDR[6], ADDR[7], ADDR[8], ADDR[9], ADDR[10], ADDR[11], ADDR[12], ADDR[13], ADDR[14], 1'b1);
  and and_4 (TTYCS, IOCS, ADDR[0], ~ADDR[1], ~ADDR[2], ~ADDR[3], ADDR[4]);  // AND_Gate
  and and_5 (KBCS, IOCS, ~ADDR[0], ~ADDR[1], ~ADDR[2], ~ADDR[3], ADDR[4]);  // AND_Gate
  and and_6 (IVECTADDR, ADDR[0], ADDR[1], ADDR[2], ADDR[3], ADDR[4], ADDR[5], ADDR[6], ADDR[7], ADDR[8], ADDR[9], ADDR[10], ADDR[11], ADDR[12], ADDR[13], ADDR[14]);
  and and_7 (TTYWR, TTYCS, WE);
  and and_8 (and_8_out, TTYWR, DATA7);
  and and_9 (KBRD, KBCS, RE);
  and and_10 (and_10_out, KBCS, WE);
  Multiplexer multiplexer_17 (.in0(and_10_out), .in1(1'b0), .out(multiplexer_17_out), .sel(KBCLR));
  and and_11 (LEDCS, IOCS, ~ADDR[4], RWE);  // AND_Gate
  and and_12 (IVECTEN, IVECTADDR, WE);
  and and_13 (IVECTRE, IVECTADDR, RE);
  or or_16 (RWE, RE, WE);
  and and_14 (MEMCS, ~IOCS, RWE);  // AND_Gate
  Multiplexer multiplexer_18 (.in0(and_8_out), .in1(1'b0), .out(multiplexer_18_out), .sel(TTYCLR));
  D_Flip_Flop d_ff_1 (.clk(CLK), .D(multiplexer_17_out), .Q(KBCLR));  // open: Qn, preset, reset
  Register #(.width(15)) register_16 (.D(CPUDATAIN), .en(IVECTEN), .Q(IVECT), .clk(CLK));  // open: clr
  D_Flip_Flop d_ff_2 (.clk(CLK), .D(multiplexer_18_out), .Q(TTYCLR));  // open: Qn, preset, reset

  assign IRQ = KBIRQ;
  assign TTYDATA = CPUDATAIN[6:0];

  // Other names for the same wires on the sheet: DATA[14:0] = CPUDATAIN; KBDATA15[7:0] = {DATA7, KBDATA}
endmodule

module ADDER15 (
  input  [14:0] A,
  input  [14:0] B,
  input  CIN,
  output COUT,
  output [14:0] S
);

  wire and_4_out, and_5_out, and_6_out, and_7_out, and_8_out, and_9_out, and_10_out, and_11_out, and_12_out,
       and_13_out, and_14_out, and_15_out, and_16_out, and_24_out, and_25_out, and_26_out, and_27_out,
       and_28_out, and_29_out, and_30_out, and_31_out, and_32_out, and_33_out, and_34_out, and_35_out,
       and_36_out, and_37_out, and_38_out, and_39_out, and_40_out, and_41_out, and_42_out, and_43_out,
       and_45_out, and_46_out, and_47_out, and_48_out, and_49_out, and_51_out, and_52_out, and_53_out,
       and_54_out, and_55_out, and_56_out, and_57_out, and_58_out, and_59_out, and_60_out, and_61_out,
       and_62_out, and_63_out, and_64_out, and_65_out, and_66_out, and_67_out, and_69_out, and_75_out,
       and_76_out, and_77_out, and_78_out, C0, C1, C2, C3, C4, C4_0, C5, C6, C7, C8, C9, C9_5, C10, C11, C12,
       C13, C14, C14_10, G0, G1, G2, G3, G4, G4_0, G5, G6, G7, G8, G9, G9_5, G10, G11, G12, G13, G14, G14_10,
       or_23_out, or_25_out, or_26_out, or_27_out, or_28_out, or_30_out, or_36_out, or_37_out, or_43_out, P0,
       P1, P2, P3, P4, P4_0, P5, P6, P7, P8, P9, P9_5, P10, P11, P12, P13, P14, P14_10;

  and and_1 (G5, A[5], B[5]);
  and and_2 (G7, A[7], B[7]);
  and and_3 (G9, A[9], B[9]);
  and and_4 (and_4_out, P0, CIN);
  and and_5 (and_5_out, A[5], B[5]);
  and and_6 (and_6_out, A[5], C4_0);
  and and_7 (and_7_out, B[5], C4_0);
  and and_8 (and_8_out, A[8], B[8]);
  and and_9 (and_9_out, A[8], C7);
  and and_10 (and_10_out, B[8], C7);
  and and_11 (and_11_out, A[10], B[10]);
  and and_12 (and_12_out, A[10], C9_5);
  and and_13 (and_13_out, B[10], C9_5);
  and and_14 (and_14_out, A[13], B[13]);
  and and_15 (and_15_out, A[13], C12);
  and and_16 (and_16_out, B[13], C12);
  and and_17 (G10, A[10], B[10]);
  and and_18 (G12, A[12], B[12]);
  and and_19 (G14, A[14], B[14]);
  ExactlyOne xor_1 (.out(S[0]), .in0(A[0]), .in1(B[0]), .in2(CIN));
  or or_1 (C0, G0, and_4_out);
  ExactlyOne xor_2 (.out(S[5]), .in0(A[5]), .in1(B[5]), .in2(C4_0));
  or or_2 (C5, and_5_out, and_6_out, and_7_out);
  ExactlyOne xor_3 (.out(S[8]), .in0(A[8]), .in1(B[8]), .in2(C7));
  or or_3 (C8, and_8_out, and_9_out, and_10_out);
  ExactlyOne xor_4 (.out(S[10]), .in0(A[10]), .in1(B[10]), .in2(C9_5));
  or or_4 (C10, and_11_out, and_12_out, and_13_out);
  ExactlyOne xor_5 (.out(S[13]), .in0(A[13]), .in1(B[13]), .in2(C12));
  or or_5 (C13, and_14_out, and_15_out, and_16_out);
  and and_20 (G6, A[6], B[6]);
  and and_21 (G8, A[8], B[8]);
  and and_22 (G11, A[11], B[11]);
  and and_23 (G13, A[13], B[13]);
  and and_24 (and_24_out, G0, P1);
  and and_25 (and_25_out, P1, P0, CIN);
  or or_6 (P5, A[5], B[5]);
  or or_7 (P7, A[7], B[7]);
  or or_8 (P9, A[9], B[9]);
  ExactlyOne xor_6 (.out(S[1]), .in0(A[1]), .in1(B[1]), .in2(C0));
  or or_9 (C1, G1, and_24_out, and_25_out);
  and and_26 (and_26_out, A[6], B[6]);
  and and_27 (and_27_out, A[6], C5);
  and and_28 (and_28_out, B[6], C5);
  and and_29 (and_29_out, A[9], B[9]);
  and and_30 (and_30_out, A[9], C8);
  and and_31 (and_31_out, B[9], C8);
  and and_32 (and_32_out, A[11], B[11]);
  and and_33 (and_33_out, A[11], C10);
  and and_34 (and_34_out, B[11], C10);
  and and_35 (and_35_out, A[14], B[14]);
  and and_36 (and_36_out, A[14], C13);
  and and_37 (and_37_out, B[14], C13);
  or or_10 (P10, A[10], B[10]);
  or or_11 (P12, A[12], B[12]);
  or or_12 (P14, A[14], B[14]);
  ExactlyOne xor_7 (.out(S[6]), .in0(A[6]), .in1(B[6]), .in2(C5));
  or or_13 (C6, and_26_out, and_27_out, and_28_out);
  ExactlyOne xor_8 (.out(S[9]), .in0(A[9]), .in1(B[9]), .in2(C8));
  or or_14 (C9, and_29_out, and_30_out, and_31_out);
  ExactlyOne xor_9 (.out(S[11]), .in0(A[11]), .in1(B[11]), .in2(C10));
  or or_15 (C11, and_32_out, and_33_out, and_34_out);
  ExactlyOne xor_10 (.out(S[14]), .in0(A[14]), .in1(B[14]), .in2(C13));
  or or_16 (C14, and_35_out, and_36_out, and_37_out);
  or or_17 (P6, A[6], B[6]);
  or or_18 (P8, A[8], B[8]);
  or or_19 (P11, A[11], B[11]);
  or or_20 (P13, A[13], B[13]);
  and and_38 (and_38_out, P2, G1);
  and and_39 (and_39_out, P2, P1, G0);
  and and_40 (and_40_out, P2, P1, P0, CIN);
  and and_41 (and_41_out, A[7], B[7]);
  and and_42 (and_42_out, A[7], C6);
  and and_43 (and_43_out, B[7], C6);
  and and_44 (P9_5, P5, P6, P7, P8, P9);
  and and_45 (and_45_out, P6, G5);
  and and_46 (and_46_out, P11, G10);
  ExactlyOne xor_11 (.out(S[2]), .in0(A[2]), .in1(B[2]), .in2(C1));
  or or_21 (C2, G2, and_38_out, and_39_out, and_40_out);
  ExactlyOne xor_12 (.out(S[7]), .in0(A[7]), .in1(B[7]), .in2(C6));
  or or_22 (C7, and_41_out, and_42_out, and_43_out);
  or or_23 (or_23_out, G6, and_45_out);
  ExactlyOne xor_13 (.out(S[12]), .in0(A[12]), .in1(B[12]), .in2(C11));
  and and_47 (and_47_out, A[12], B[12]);
  and and_48 (and_48_out, A[12], C11);
  or or_24 (C12, and_47_out, and_48_out, and_49_out);
  and and_49 (and_49_out, B[12], C11);
  and and_50 (P14_10, P10, P11, P12, P13, P14);
  or or_25 (or_25_out, G11, and_46_out);
  or or_26 (or_26_out, G7, and_51_out);
  and and_51 (and_51_out, P7, or_23_out);
  and and_52 (and_52_out, P12, or_25_out);
  and and_53 (and_53_out, P8, or_26_out);
  or or_27 (or_27_out, G12, and_52_out);
  and and_54 (and_54_out, P3, G2);
  and and_55 (and_55_out, P3, P2, G1);
  and and_56 (and_56_out, P3, P2, P1, G0);
  and and_57 (and_57_out, P3, P2, P1, P0, CIN);
  or or_28 (or_28_out, G8, and_53_out);
  and and_58 (and_58_out, P13, or_27_out);
  ExactlyOne xor_14 (.out(S[3]), .in0(A[3]), .in1(B[3]), .in2(C2));
  or or_29 (C3, G3, and_54_out, and_55_out, and_56_out, and_57_out);
  and and_59 (and_59_out, P9, or_28_out);
  and and_60 (and_60_out, P14, or_30_out);
  or or_30 (or_30_out, G13, and_58_out);
  or or_31 (G9_5, G9, and_59_out);
  or or_32 (G14_10, G14, and_60_out);
  and and_61 (and_61_out, P4, G3);
  and and_62 (and_62_out, P4, P3, G2);
  and and_63 (and_63_out, P4, P3, P2, G1);
  and and_64 (and_64_out, P4, P3, P2, P1, G0);
  and and_65 (and_65_out, P4, P3, P2, P1, P0, CIN);
  and and_66 (and_66_out, P9_5, C4_0);
  ExactlyOne xor_15 (.out(S[4]), .in0(A[4]), .in1(B[4]), .in2(C3));
  or or_33 (C4, G4, and_61_out, and_62_out, and_63_out, and_64_out, and_65_out);
  or or_34 (C9_5, G9_5, and_66_out);
  and and_67 (and_67_out, P14_10, C9_5);
  or or_35 (C14_10, G14_10, and_67_out);
  and and_68 (P4_0, P0, P1, P2, P3, P4);
  or or_36 (or_36_out, G1, and_69_out);
  and and_69 (and_69_out, P1, G0);
  and and_70 (G0, A[0], B[0]);
  and and_71 (G1, A[1], B[1]);
  and and_72 (G2, A[2], B[2]);
  and and_73 (G3, A[3], B[3]);
  and and_74 (G4, A[4], B[4]);
  and and_75 (and_75_out, P2, or_36_out);
  or or_37 (or_37_out, G2, and_75_out);
  and and_76 (and_76_out, P3, or_37_out);
  or or_38 (P0, A[0], B[0]);
  or or_39 (P1, A[1], B[1]);
  or or_40 (P2, A[2], B[2]);
  or or_41 (P3, A[3], B[3]);
  or or_42 (P4, A[4], B[4]);
  or or_43 (or_43_out, G3, and_76_out);
  and and_77 (and_77_out, P4, or_43_out);
  or or_44 (G4_0, G4, and_77_out);
  and and_78 (and_78_out, P4_0, CIN);
  or or_45 (C4_0, G4_0, and_78_out);

  // Notes on the sheet:
  //   Bits 5-9
  //   Bits 10-14
  //   Bits 0-4
  //   CLA Logic
endmodule

module REGS15 (
  input  [14:0] D,
  input  W,
  input  [2:0] SelD,
  input  CLK,
  input  [2:0] SelA,
  input  [2:0] SelB,
  output [14:0] R0,
  output [14:0] R1,
  output [14:0] R2,
  output [14:0] R3,
  output [14:0] R4,
  output [14:0] R5,
  output [14:0] R6,
  output [14:0] R7,
  output [14:0] A,
  output [14:0] B
);
endmodule

module ALU15 (
  input  [14:0] A,
  input  [14:0] B,
  input  [2:0] OP,
  input  CIN,
  input  OIN,
  output C,
  output O,
  output N,
  output Z,
  output [14:0] R
);
endmodule

module FLAGS8 (
  input  IRQ,
  input  [7:0] NF,
  input  [7:0] WM,
  input  CLK,
  output [7:0] F
);
endmodule

module IMM15 (
  input  [14:0] INST,
  output [14:0] SEXT
);
endmodule

module DECODE15 (
  input  [4:0] OPCODE,
  output SWI,
  output STORE,
  output LOAD,
  output [1:0] ASEL,
  output [1:0] BSEL,
  output [2:0] ALUOP,
  output [2:0] REGDATASRC,
  output REGW,
  output [1:0] FLAGSRC,
  output [7:0] FLAGWM,
  output SRPW,
  output SRFW
);
endmodule
